# Fritzing sketch 20141116_tape_cleaner (saved by Fritzing 0.9.0b)
breadboards: 1

parts:
  Arduino_Uno = Arduino Uno (Rev3)
  Motor_Shield = Arduino Motor Shield (Rev3)
  M1 = DC Motor [part_number="supply motor A"]
  VCC1 = Battery block 9V [part_number="12V power source"]
  S2 = SWITCH-DPDT [part_number="A/B wind switch" package=ms]
  M2 = DC Motor [part_number="takeup motor B"]  # not connected
  S1 = SPST Switch [part_number="on/off switch" package=switche-dpdt]  # not connected

nets (from the breadboard view):
  N1: Arduino_Uno.A0, Motor_Shield.A0
  N2: Arduino_Uno.A1, Motor_Shield.A1
  N3: Arduino_Uno.A2, Motor_Shield.A2
  N4: Arduino_Uno.A3, Motor_Shield.A3
  N5: Arduino_Uno.A4/SDA, Motor_Shield.A4, Motor_Shield.SDA
  N6: Arduino_Uno.A5/SCL, Motor_Shield.A5, Motor_Shield.SCL
  N7: Arduino_Uno.D8, Motor_Shield.D8/BreakeB
  N8: Arduino_Uno.D9_PWM, Motor_Shield.D9/BreakeA
  N9: Arduino_Uno.D10_PWM/SS, Motor_Shield.D10_PWM
  N10: Arduino_Uno.D11_PWM/MOSI, Motor_Shield.D11_PWM/B
  N11: Arduino_Uno.D12/MISO, Motor_Shield.D12/DirA
  N12: Arduino_Uno.D13/SCK, Motor_Shield.D13/DirB
  GND: Arduino_Uno.GND, Motor_Shield.GND, VCC1.-
  N13: Arduino_Uno.AREF, Motor_Shield.AREF
  N14: Arduino_Uno.D0/RX, Motor_Shield.IOREF#118
  N15: Arduino_Uno.D1/TX, Motor_Shield.D1/TX
  N16: Arduino_Uno.D2, Motor_Shield.D2
  N17: Arduino_Uno.D3_PWM, Motor_Shield.D3_PWM/A
  N18: Arduino_Uno.D4, Motor_Shield.D4
  N19: Arduino_Uno.D5_PWM, Motor_Shield.D5_PWM
  N20: Arduino_Uno.D6_PWM, Motor_Shield.D6_PWM
  N21: Arduino_Uno.D7, Motor_Shield.D7
  N22: Arduino_Uno.ioref, Motor_Shield.IOREF#147
  N23: Arduino_Uno.RESET, Motor_Shield.RESET
  3V3: Arduino_Uno.3V3, Motor_Shield.3V3
  5V: Arduino_Uno.5V, Motor_Shield.5V
  VIN: Arduino_Uno.VIN, Motor_Shield.VIN
  N24: Motor_Shield.B-, S2.3
  N25: Motor_Shield.B+, S2.1, S2.2
  N26: Motor_Shield.A-, M1.pin_2
  N27: Motor_Shield.A+, M1.pin_1
