# Fritzing sketch tape_cleaner (saved by Fritzing 0.9.0b)
breadboards: 1

parts:
  Part1 = Arduino Uno (Rev3)
  Part2 = Arduino Motor Shield (Rev3)
  Part3 = Arduino Motor Shield (Rev3)
  M1 = DC Motor
  M2 = DC Motor
  M3 = DC Motor
  M4 = DC Motor

nets:
  N1: Part1.A0, Part2.A0, Part3.A0
  N2: Part1.A1, Part2.A1, Part3.A1
  N3: Part1.A2, Part2.A2, Part3.A2
  N4: Part1.A3, Part2.A3, Part3.A3
  N5: Part1.A4/SDA, Part2.A4, Part2.SDA, Part3.A4
  N6: Part1.A5/SCL, Part2.A5, Part2.SCL, Part3.A5
  N7: Part1.D8, Part2.D8/BreakeB
  N8: Part1.D9_PWM, Part2.D9/BreakeA
  N9: Part1.D10_PWM/SS, Part2.D10_PWM
  N10: Part1.D11_PWM/MOSI, Part2.D11_PWM/B
  N11: Part1.D12/MISO, Part2.D12/DirA
  N12: Part1.D13/SCK, Part2.D13/DirB
  GND: Part1.GND, Part2.GND, Part3.GND
  N13: Part1.AREF, Part2.AREF
  N14: Part1.D0/RX, Part2.IOREF#118, Part3.IOREF#118
  N15: Part1.D1/TX, Part2.D1/TX, Part3.D1/TX
  N16: Part1.D2, Part2.D2
  N17: Part1.D3_PWM, Part2.D3_PWM/A
  N18: Part1.D4, Part2.D4
  N19: Part1.D5_PWM, Part2.D5_PWM
  N20: Part1.D6_PWM, Part2.D6_PWM
  N21: Part1.D7, Part2.D7
  N22: Part1.ioref, Part2.IOREF#147, Part3.IOREF#147
  N23: Part1.RESET, Part2.RESET, Part3.RESET
  3V3: Part1.3V3, Part2.3V3, Part3.3V3
  5V: Part1.5V, Part2.5V, Part3.5V
  VIN: Part1.VIN, Part2.VIN, Part3.VIN
  N24: Part2.B-, M1.pin_2
  N25: Part2.B+, M1.pin_1
  N26: Part2.A-, M2.pin_2
  N27: Part2.A+, M2.pin_1
  N28: Part3.B-, M3.pin_2
  N29: Part3.B+, M3.pin_1
  N30: Part3.A-, M4.pin_2
  N31: Part3.A+, M4.pin_1
