# Fritzing sketch 20141115_tape_cleaner (saved by Fritzing 0.9.0b)
breadboards: 1

parts:
  Part1 = Arduino Uno (Rev3)
  Part2 = Arduino Motor Shield (Rev3)
  M1 = DC Motor
  M2 = DC Motor
  VCC1 = Battery block 9V
  S1 = Square Pushbutton

nets:
  N1: Part1.A0, Part2.A0
  N2: Part1.A1, Part2.A1
  N3: Part1.A2, Part2.A2
  N4: Part1.A3, Part2.A3
  N5: Part1.A4/SDA, Part2.A4, Part2.SDA
  N6: Part1.A5/SCL, Part2.A5, Part2.SCL
  N7: Part1.D8, Part2.D8/BreakeB
  N8: Part1.D9_PWM, Part2.D9/BreakeA
  N9: Part1.D10_PWM/SS, Part2.D10_PWM
  N10: Part1.D11_PWM/MOSI, Part2.D11_PWM/B
  N11: Part1.D12/MISO, Part2.D12/DirA
  N12: Part1.D13/SCK, Part2.D13/DirB
  GND: Part1.GND, Part2.GND, VCC1.-, S1.leg0
  N13: Part1.AREF, Part2.AREF
  N14: Part1.D0/RX, Part2.IOREF#118
  N15: Part1.D1/TX, Part2.D1/TX
  N16: Part1.D2, Part2.D2
  N17: Part1.D3_PWM, Part2.D3_PWM/A
  N18: Part1.D4, Part2.D4
  N19: Part1.D5_PWM, Part2.D5_PWM
  N20: Part1.D6_PWM, Part2.D6_PWM
  N21: Part1.D7, Part2.D7
  N22: Part1.ioref, Part2.IOREF#147
  N23: Part1.RESET, Part2.RESET
  3V3: Part1.3V3, Part2.3V3
  5V: Part1.5V, Part2.5V
  VIN: Part1.VIN, Part2.VIN
  N24: Part2.B-, M1.pin_2
  N25: Part2.B+, M1.pin_1
  N26: Part2.A-, M2.pin_2
  N27: Part2.A+, M2.pin_1
  N28: Part2.VMOT, VCC1.+, S1.leg1
